// Digital circuit 4bit_CPU.dig as structural Verilog
module _4bit_CPU (
);

  gp_register A ();  // open: Ctrl, In, Clk, Q, Qinv
  gp_register B ();  // open: Ctrl, In, Clk, Q, Qinv
  gp_register IR ();  // open: Ctrl, In, Clk, Q, Qinv
endmodule
